# Fritzing sketch digital-clock (saved by Fritzing 0.9.4)
breadboards: 1

parts:
  Part2 = Arduino Uno (Rev3) - ICSP
  Grove1 = Grove OLED 128x96
  S2 = Pushbutton [package="[THT]"]
  S3 = Pushbutton [package="[THT]"]

nets:
  N1: Part2.A4/SDA, Grove1.SDA
  N2: Part2.A5/SCL, Grove1.SCL
  GND: Part2.GND, Grove1.GND, S2.Pin_1, S2.Pin_2, S3.Pin_1, S3.Pin_2
  N3: Part2.D2, S3.Pin_3, S3.Pin_4
  N4: Part2.D3_PWM, S2.Pin_3, S2.Pin_4
  5V: Part2.5V, Grove1.VCC
